# Fritzing sketch arduino_multiple_steppers (saved by Fritzing 0.9.3b)
breadboards: 1

parts:
  Pololu_A1 = Pololu A4988 [package=SO16]
  M1 = Stepper Motor - Bipolar
  C1 = Electrolytic Capacitor [capacitance=100μF package="0807 [SMD, electrolytic]"]
  Power_plug1 = Power plug
  Part1 = Arduino Mega 2560 (Rev3)
  M2 = Stepper Motor - Bipolar
  Pololu_A2 = Pololu A4988 [package=SO16]
  C2 = Electrolytic Capacitor [capacitance=100μF package="0807 [SMD, electrolytic]"]

nets:
  N1: Pololu_A1.RESET, Pololu_A1.SLEEP
  N2: Pololu_A1.STEP, Part1.D52
  N3: Pololu_A1.DIR, Part1.D53
  N4: Pololu_A1.GND#8, Part1.GND, Pololu_A2.GND#8
  VDD: Pololu_A1.VDD, Part1.5V, Pololu_A2.VDD
  N5: Pololu_A1.1B, M1.D
  N6: Pololu_A1.1A, M1.B
  N7: Pololu_A1.2A, M1.C
  N8: Pololu_A1.2B, M1.A
  N9: Pololu_A1.GND#14, C1.-, Power_plug1.GND, Pololu_A2.GND#14, C2.-
  N10: Pololu_A1.VMOT, C1.+, Power_plug1.VCC, Pololu_A2.VMOT, C2.+
  N11: Part1.D50, Pololu_A2.STEP
  N12: Part1.D51, Pololu_A2.DIR
  N13: M2.A, Pololu_A2.2B
  N14: M2.C, Pololu_A2.2A
  N15: M2.B, Pololu_A2.1A
  N16: M2.D, Pololu_A2.1B
  N17: Pololu_A2.RESET, Pololu_A2.SLEEP

notes:
  A4988 Module
  100μF Capacitor (mount the capacitor as close to the A4988 V and GND pins as possible)
  12V Power Supply
  Logic supply V and GND
  Motor supply
  V and GND
  Bipolar stepper
  2.1 mm barrel connector can be supplied with 7V - 12V (https://www.technobyte.org/2016/07/power-up-the-arduino-uno/)
