# Fritzing sketch arduino_stepper_A4988 (saved by Fritzing 0.9.3b)
breadboards: 1

parts:
  Pololu_A1 = Pololu A4988 [package=SO16]
  M1 = Stepper Motor - Bipolar
  Part1 = Arduino Uno (Rev3) - ICSP
  C1 = Electrolytic Capacitor [capacitance=100μF package="0807 [SMD, electrolytic]"]
  Power_plug1 = Power plug

nets:
  N1: Pololu_A1.RESET, Pololu_A1.SLEEP
  N2: Pololu_A1.STEP, Part1.D3_PWM
  N3: Pololu_A1.DIR, Part1.D2
  N4: Pololu_A1.GND#8, Part1.GND
  VDD: Pololu_A1.VDD, Part1.5V
  N5: Pololu_A1.1B, M1.C
  N6: Pololu_A1.1A, M1.D
  N7: Pololu_A1.2A, M1.B
  N8: Pololu_A1.2B, M1.A
  N9: Pololu_A1.GND#14, C1.-, Power_plug1.GND
  N10: Pololu_A1.VMOT, C1.+, Power_plug1.VCC

notes:
  A4988 Module
  100μF Capacitor (mount the capacitor as close to the A4988 V and GND pins as possible)
  STEP
  DIR
  12V Power Supply
  Logic supply V and GND
  Motor supply
  V and GND
  Bipolar stepper
  Coil 1 pins
  Coil 2 pins
