# Fritzing sketch arduino_stepper_A4988_encoder_switches (saved by Fritzing 0.9.3b)
breadboards: 1

parts:
  Pololu_A1 = Pololu A4988 [package=SO16]
  M1 = Stepper Motor - Bipolar
  Part1 = Arduino Uno (Rev3) - ICSP
  C1 = Electrolytic Capacitor [capacitance=100μF package="0807 [SMD, electrolytic]"]
  Power_plug1 = Power plug
  ENCODER2 = Rotary Encoder with Knob
  S1 = Toggle Switch [package=THT]
  S2 = Toggle Switch [package=THT]

nets:
  N1: Pololu_A1.RESET, Pololu_A1.SLEEP
  N2: Pololu_A1.STEP, Part1.D9_PWM
  N3: Pololu_A1.DIR, Part1.D8
  N4: Pololu_A1.GND#8, Part1.GND, S1.L2, S2.L2
  VDD: Pololu_A1.VDD, Part1.5V
  N5: Pololu_A1.1B, M1.C
  N6: Pololu_A1.1A, M1.D
  N7: Pololu_A1.2A, M1.B
  N8: Pololu_A1.2B, M1.A
  N9: Pololu_A1.GND#14, C1.-, Power_plug1.GND
  N10: Pololu_A1.VMOT, C1.+, Power_plug1.VCC
  N11: Part1.D11_PWM/MOSI, S1.COM
  N12: Part1.D12/MISO, S2.COM
  N13: Part1.D2, ENCODER2.no_name_yet#3
  N14: Part1.D3_PWM, ENCODER2.no_name_yet#1
  N15: Part1.D4, ENCODER2.no_name_yet#4

notes:
  A4988 Module
  100μF Capacitor (mount the capacitor as close to the A4988 V and GND pins as possible)
  STEP
  DIR
  12V Power Supply
  Logic supply V and GND
  Motor supply
  V and GND
  Bipolar stepper
  Coil 1 pins
  Coil 2 pins
  2.1 mm barrel connector can be supplied with 7V - 12V (https://www.technobyte.org/2016/07/power-up-the-arduino-uno/)
  Limit switch pins: NC, NO, COM

custom parts:
  Rotary Encoder with Knob: Rotary Encoder with 1/4" Shaft and Knob
