# Fritzing sketch arduino_stepper_DRV8825 (saved by Fritzing 0.9.3b)
breadboards: 1

parts:
  M1 = Stepper Motor - Bipolar  # not connected
  Part1 = Arduino Uno (Rev3) - ICSP  # not connected
  C1 = Electrolytic Capacitor [capacitance=100μF package="0807 [SMD, electrolytic]"]
  Power_plug1 = Power plug
  DRV_1 = DRV 8825 Stepper Motor Carrier, High Current [part_number="DRV 8825"]  # not connected

nets:
  N1: C1.-, Power_plug1.GND
  N2: C1.+, Power_plug1.VCC

notes:
  DRV8825 Module
  100μF Capacitor (mount the capacitor as close to the A4988 V and GND pins as possible)
  STEP
  DIR
  12V Power Supply
  Logic supply V and GND
  Motor supply
  V and GND
  Bipolar stepper
  Coil 1 pins
  Coil 2 pins
